# Fritzing sketch display16 (saved by Fritzing 0.8.3b)
perfboards: 1

parts:
  U1 = Alphanumeric LED Display [package=alphanumeric]
  IC1 = IC, DIP package, 22 pins [chip_label=MM5484N]
  R2 = Resistor [tolerance=±5% resistance=470 package=THT]
  R3 = Resistor [tolerance=±5% resistance=470 package=THT]
  R4 = Resistor [tolerance=±5% resistance=470 package=THT]
  R5 = Resistor [tolerance=±5% resistance=470 package=THT]
  R6 = Resistor [tolerance=±5% resistance=470 package=THT]
  R7 = Resistor [tolerance=±5% resistance=470 package=THT]
  R13 = Resistor [tolerance=±5% resistance=390 package=THT]
  R15 = Resistor [tolerance=±5% resistance=390 package=THT]
  R16 = Resistor [tolerance=±5% resistance=390 package=THT]
  R17 = Resistor [tolerance=±5% resistance=390 package=THT]
  R18 = Resistor [tolerance=±5% resistance=390 package=THT]
  R19 = Resistor [tolerance=±5% resistance=390 package=THT]
  R20 = Resistor [tolerance=±5% resistance=390 package=THT]
  R21 = Resistor [tolerance=±5% resistance=390 package=THT]
  R22 = Resistor [tolerance=±5% resistance=390 package=THT]
  R23 = Resistor [tolerance=±5% resistance=390 package=THT]
  J1 = screw terminal, 6 pins
  J2 = screw terminal, 6 pins

nets:
  N1: U1.NC, R20.Pin_0
  N2: U1.A1, R6.Pin_0
  N3: U1.F, R21.Pin_0
  N4: U1.VCC, J1.pin1, J2.pin6
  N5: U1.G1, R7.Pin_0
  N6: U1.E, R19.Pin_0
  N7: U1.D1, R5.Pin_0
  N8: U1.N, R23.Pin_0
  N9: U1.M, R22.Pin_0
  N10: U1.D2, R2.Pin_1
  N11: U1.L, R16.Pin_1
  N12: U1.C, R15.Pin_1
  N13: U1.G2, R3.Pin_1
  N14: U1.B, R17.Pin_1
  N15: U1.A2, R4.Pin_1
  N16: U1.K, R18.Pin_1
  N17: U1.J, R13.Pin_1
  N18: IC1.pin1, R5.Pin_1
  N19: IC1.pin2, R7.Pin_1
  N20: IC1.pin3, R6.Pin_1
  N21: IC1.pin4, R22.Pin_1
  N22: IC1.pin5, J2.pin1
  N23: IC1.pin6, J1.pin2, J2.pin5
  N24: IC1.pin7, J1.pin6
  N25: IC1.pin8, R23.Pin_1
  N26: IC1.pin9, R19.Pin_1
  N27: IC1.pin10, R21.Pin_1
  N28: IC1.pin11, R20.Pin_1
  N29: IC1.pin12, R13.Pin_0
  N30: IC1.pin13, R18.Pin_0
  N31: IC1.pin14, R17.Pin_0
  N32: IC1.pin15, R15.Pin_0
  N33: IC1.pin16, J1.pin3, J2.pin4
  N34: IC1.pin17, J1.pin5, J2.pin2
  N35: IC1.pin18, J1.pin4, J2.pin3
  N36: IC1.pin19, R16.Pin_0
  N37: IC1.pin20, R4.Pin_0
  N38: IC1.pin21, R3.Pin_0
  N39: IC1.pin22, R2.Pin_0

notes:
  data in
  enable
  clock
  ground
  5v
  9v
